# Fritzing sketch Aquarium (saved by Fritzing 0.9.3b)
breadboards: 1

parts:
  Part1 = Arduino Nano (Rev3.0)  # not connected
  LED1 = LED - 5mm [color="Red (633nm)" package="5 mm [THT]"]  # not connected
  DS1 = DS18B20 1-Wire Temperature Sensor [part_number=DS18B20]
  Grove1 = Grove OLED 128x96  # not connected
  R1 = Resistor [tolerance=±5% resistance=220 package="0805 [SMD]"]

nets:
  N1: DS1.DQ, R1.Pin_0
  N2: DS1.VDD, R1.Pin_1
